# Fritzing sketch Nucleo-Bipolar-Steppingmotor (saved by Fritzing 0.9.3b)
circuit board: 8.46667cm x 5.64444cm
breadboards: 1

parts:
  Pololu_A1 = Pololu A4988 [package=SO16]
  HLK-PM1 = HLK-PM12 [part_number=HLK-PM12]
  M1 = Stepper Motor - Bipolar
  J1 = STM32 Nucleo boards

nets:
  N1: Pololu_A1.RESET, Pololu_A1.SLEEP
  N2: Pololu_A1.STEP, J1.D5_PWM
  N3: Pololu_A1.DIR, J1.D4
  N4: Pololu_A1.GND#8, J1.GND
  VDD: Pololu_A1.VDD, J1.5V
  N5: Pololu_A1.1B, M1.B
  N6: Pololu_A1.1A, M1.A
  N7: Pololu_A1.2A, M1.C
  N8: Pololu_A1.2B, M1.D
  N9: Pololu_A1.GND#14, HLK-PM1.-Vo
  N10: Pololu_A1.VMOT, HLK-PM1.+Vo
